// Logisim project assign1.circ as structural Verilog: 10 circuits, main circuit main
module main (
  input  w,
  input  x,
  input  y,
  input  z
);

  wire a_1_a, b_1_b, c_1_c, d_1_d, e_1_e, f_1_f, g_1_g, h_1_h, i_1_i;

  A a_1 (.w(w), .x(x), .y(y), .z(z), .A(a_1_a));
  B b_1 (.w(w), .x(x), .y(y), .z(z), .B(b_1_b));
  C c_1 (.w(w), .x(x), .y(y), .z(z), .C(c_1_c));
  D d_1 (.w(w), .x(x), .y(y), .z(z), .D(d_1_d));
  E e_1 (.w(w), .x(x), .y(y), .z(z), .E(e_1_e));
  F f_1 (.w(w), .x(x), .y(y), .z(z), .F(f_1_f));
  G g_1 (.w(w), .x(x), .y(y), .z(z), .G(g_1_g));
  H h_1 (.w(w), .x(x), .y(y), .z(z), .H(h_1_h));
  I i_1 (.w(w), .x(x), .y(y), .z(z), .I(i_1_i));
  LED led_1 (.in(a_1_a));
  LED led_2 (.in(d_1_d));
  LED led_3 (.in(g_1_g));
  LED led_4 (.in(b_1_b));
  LED led_5 (.in(c_1_c));
  LED led_6 (.in(f_1_f));
  LED led_7 (.in(e_1_e));
  LED led_8 (.in(i_1_i));
  LED led_9 (.in(h_1_h));
endmodule

module A (
  input  w,
  input  x,
  input  y,
  input  z,
  output A
);

  wire and_1_out, and_2_out, and_3_out, and_4_out, and_5_out, not_1_out, not_2_out, not_3_out, not_4_out;

  not not_1 (not_1_out, w);
  not not_2 (not_2_out, x);
  not not_3 (not_3_out, y);
  not not_4 (not_4_out, z);
  and and_1 (and_1_out, w, not_2_out, z);
  and and_2 (and_2_out, w, x, not_4_out);
  and and_3 (and_3_out, not_2_out, not_3_out, not_4_out);
  and and_4 (and_4_out, not_1_out, y, z);
  and and_5 (and_5_out, w, not_3_out);
  or or_1 (A, and_1_out, and_2_out, and_3_out, and_4_out, and_5_out);
endmodule

module B (
  input  w,
  input  x,
  input  y,
  input  z,
  output B
);

  wire and_1_out, and_2_out, and_3_out, and_4_out, not_1_out, not_2_out, not_3_out, not_4_out;

  not not_1 (not_1_out, w);
  not not_2 (not_2_out, x);
  not not_3 (not_3_out, y);
  not not_4 (not_4_out, z);
  and and_1 (and_1_out, not_1_out, not_3_out, not_4_out);
  and and_2 (and_2_out, w, y, not_4_out);
  and and_3 (and_3_out, w, not_2_out, y);
  and and_4 (and_4_out, w, not_2_out, not_4_out);
  or or_1 (B, and_1_out, and_2_out, and_3_out, and_4_out);
endmodule

module C (
  input  w,
  input  x,
  input  y,
  input  z,
  output C
);

  wire and_1_out, and_2_out, and_3_out, and_4_out, and_5_out, not_2_out, not_3_out, not_4_out;

  // NOT_Gate not_1 has open pins: in=w, out=open
  not not_2 (not_2_out, x);
  not not_3 (not_3_out, y);
  not not_4 (not_4_out, z);
  and and_1 (and_1_out, w, not_3_out);
  and and_2 (and_2_out, not_2_out, not_3_out, not_4_out);
  and and_3 (and_3_out, x, not_3_out, z);
  and and_4 (and_4_out, w, not_2_out, z);
  and and_5 (and_5_out, x, y, not_4_out);
  or or_1 (C, and_1_out, and_2_out, and_3_out, and_4_out, and_5_out);
endmodule

module D (
  input  w,
  input  x,
  input  y,
  input  z,
  output D
);

  wire and_1_out, and_2_out, and_3_out, and_4_out, not_1_out, not_2_out, not_3_out, not_4_out;

  not not_1 (not_1_out, w);
  not not_2 (not_2_out, x);
  not not_3 (not_3_out, y);
  not not_4 (not_4_out, z);
  and and_1 (and_1_out, not_1_out, not_2_out, z);
  and and_2 (and_2_out, w, y, not_4_out);
  and and_3 (and_3_out, w, x, not_4_out);
  and and_4 (and_4_out, not_2_out, not_3_out, z);
  or or_1 (D, and_1_out, and_2_out, and_3_out, and_4_out);
endmodule

module E (
  input  w,
  input  x,
  input  y,
  input  z,
  output E
);

  wire and_1_out, and_2_out, and_3_out, and_4_out, and_5_out, not_1_out, not_2_out, not_3_out, not_4_out;

  not not_1 (not_1_out, w);
  not not_2 (not_2_out, x);
  not not_3 (not_3_out, y);
  not not_4 (not_4_out, z);
  and and_1 (and_1_out, not_1_out, not_2_out, not_3_out, z);
  and and_2 (and_2_out, not_1_out, x, not_4_out);
  and and_3 (and_3_out, x, y, z);
  and and_4 (and_4_out, w, x, not_3_out);
  and and_5 (and_5_out, w, not_2_out, y);
  or or_1 (E, and_1_out, and_2_out, and_3_out, and_4_out, and_5_out);
endmodule

module F (
  input  w,
  input  x,
  input  y,
  input  z,
  output F
);

  wire and_1_out, and_2_out, and_3_out, and_4_out, not_1_out, not_2_out, not_3_out, not_4_out;

  not not_1 (not_1_out, w);
  not not_2 (not_2_out, x);
  not not_3 (not_3_out, y);
  not not_4 (not_4_out, z);
  and and_1 (and_1_out, not_1_out, not_3_out, z);
  and and_2 (and_2_out, w, y, not_4_out);
  and and_3 (and_3_out, w, x, not_4_out);
  and and_4 (and_4_out, not_2_out, not_3_out, z);
  or or_1 (F, and_1_out, and_2_out, and_3_out, and_4_out);
endmodule

module G (
  input  w,
  input  x,
  input  y,
  input  z,
  output G
);

  wire and_1_out, and_2_out, and_3_out, and_4_out, not_1_out, not_2_out, not_3_out, not_4_out;

  not not_1 (not_1_out, w);
  not not_2 (not_2_out, x);
  not not_3 (not_3_out, y);
  not not_4 (not_4_out, z);
  and and_1 (and_1_out, not_1_out, not_2_out, y);
  and and_2 (and_2_out, w, not_3_out);
  and and_3 (and_3_out, x, y, not_4_out);
  and and_4 (and_4_out, w, not_2_out, z);
  or or_1 (G, and_1_out, and_2_out, and_3_out, and_4_out);
endmodule

module H (
  input  w,
  input  x,
  input  y,
  input  z,
  output H
);

  wire and_1_out, and_2_out, and_3_out, and_4_out, and_5_out, not_1_out, not_2_out, not_3_out, not_4_out;

  not not_1 (not_1_out, w);
  not not_2 (not_2_out, x);
  not not_3 (not_3_out, y);
  not not_4 (not_4_out, z);
  and and_1 (and_1_out, not_1_out, x, not_3_out, not_4_out);
  and and_2 (and_2_out, w, not_2_out, not_4_out);
  and and_3 (and_3_out, w, not_2_out, y);
  and and_4 (and_4_out, w, y, not_4_out);
  and and_5 (and_5_out, not_2_out, y, not_4_out);
  or or_1 (H, and_1_out, and_2_out, and_3_out, and_4_out, and_5_out);
endmodule

module I (
  input  w,
  input  x,
  input  y,
  input  z,
  output I
);

  wire and_1_out, and_2_out, and_3_out, and_4_out, and_5_out, not_1_out, not_2_out, not_3_out, not_4_out;

  not not_1 (not_1_out, w);
  not not_2 (not_2_out, x);
  not not_3 (not_3_out, y);
  not not_4 (not_4_out, z);
  and and_1 (and_1_out, not_1_out, not_2_out, y, not_4_out);
  and and_2 (and_2_out, not_1_out, x, z);
  and and_3 (and_3_out, w, not_3_out);
  and and_4 (and_4_out, w, x, not_4_out);
  and and_5 (and_5_out, w, not_2_out, z);
  or or_1 (I, and_1_out, and_2_out, and_3_out, and_4_out, and_5_out);
endmodule
