// Logisim project backup.circ as structural Verilog: 10 circuits, main circuit main
module main (
  input  w,
  input  x,
  input  y,
  input  w_2,
  input  w_3,
  input  z,
  input  x_2,
  input  x_3,
  input  w_4,
  input  y_2,
  input  y_3,
  input  x_4,
  input  z_2,
  input  z_3,
  input  y_4,
  input  w_5,
  input  z_4,
  input  x_5,
  input  y_5,
  input  z_5,
  input  w_6,
  input  x_6,
  input  w_7,
  input  y_6,
  input  x_7,
  input  z_6,
  input  y_7,
  input  z_7,
  input  w_8,
  input  x_8,
  input  w_9,
  input  y_8,
  input  x_9,
  input  z_8,
  input  y_9,
  input  z_9,
  input  w_10,
  input  x_10,
  input  w_11,
  input  y_10,
  input  x_11,
  input  z_10,
  input  y_11,
  input  z_11,
  output out_45,
  output I,
  output out_47,
  output A,
  output out_49,
  output F,
  output out_51,
  output G,
  output out_53,
  output H,
  output out_55
);

  wire and_1_out, and_2_out, and_3_out, and_4_out, and_5_out, and_6_out, and_7_out, and_8_out, and_9_out,
       and_10_out, and_11_out, and_12_out, and_13_out, and_14_out, and_15_out, and_16_out, and_17_out,
       and_18_out, and_19_out, and_20_out, and_21_out, and_22_out, and_23_out, and_24_out, and_25_out,
       and_26_out, and_27_out, and_28_out, and_29_out, and_30_out, and_31_out, and_32_out, and_33_out,
       and_34_out, and_35_out, and_36_out, and_37_out, and_38_out, and_39_out, and_40_out, and_41_out,
       and_42_out, and_43_out, and_44_out, and_45_out, and_46_out, and_47_out, and_48_out, and_49_out,
       not_1_out, not_2_out, not_3_out, not_4_out, not_5_out, not_6_out, not_7_out, not_8_out, not_10_out,
       not_11_out, not_12_out, not_13_out, not_14_out, not_15_out, not_16_out, not_17_out, not_18_out,
       not_19_out, not_20_out, not_21_out, not_22_out, not_23_out, not_24_out, not_25_out, not_26_out,
       not_27_out, not_28_out, not_29_out, not_30_out, not_31_out, not_32_out, not_33_out, not_34_out,
       not_35_out, not_36_out;

  not not_1 (not_1_out, w_4);
  not not_2 (not_2_out, x_4);
  not not_3 (not_3_out, y_4);
  not not_4 (not_4_out, z_4);
  not not_5 (not_5_out, w_7);
  not not_6 (not_6_out, x_7);
  not not_7 (not_7_out, y_7);
  not not_8 (not_8_out, z_7);
  // NOT_Gate not_9 has open pins: in=w_9, out=open
  not not_10 (not_10_out, x_9);
  not not_11 (not_11_out, y_9);
  not not_12 (not_12_out, z_9);
  not not_13 (not_13_out, w_11);
  not not_14 (not_14_out, x_11);
  not not_15 (not_15_out, y_11);
  not not_16 (not_16_out, z_11);
  and and_1 (and_1_out, w_4, not_2_out, z_4);
  and and_2 (and_2_out, w_4, x_4, not_4_out);
  and and_3 (and_3_out, not_2_out, not_3_out, not_4_out);
  and and_4 (and_4_out, not_1_out, y_4, z_4);
  and and_5 (and_5_out, w_4, not_3_out);
  and and_6 (and_6_out, not_5_out, not_7_out, not_8_out);
  and and_7 (and_7_out, w_7, y_7, not_8_out);
  and and_8 (and_8_out, w_7, not_6_out, y_7);
  and and_9 (and_9_out, w_7, not_6_out, not_8_out);
  and and_10 (and_10_out, w_9, not_11_out);
  and and_11 (and_11_out, not_10_out, not_11_out, not_12_out);
  and and_12 (and_12_out, x_9, not_11_out, z_9);
  and and_13 (and_13_out, w_9, not_10_out, z_9);
  and and_14 (and_14_out, x_9, y_9, not_12_out);
  and and_15 (and_15_out, not_13_out, not_14_out, z_11);
  and and_16 (and_16_out, w_11, y_11, not_16_out);
  and and_17 (and_17_out, w_11, x_11, not_16_out);
  and and_18 (and_18_out, not_14_out, not_15_out, z_11);
  or or_1 (A, and_1_out, and_2_out, and_3_out, and_4_out, and_5_out);
  or or_2 (out_51, and_6_out, and_7_out, and_8_out, and_9_out);
  or or_3 (out_53, and_10_out, and_11_out, and_12_out, and_13_out, and_14_out);
  or or_4 (out_55, and_15_out, and_16_out, and_17_out, and_18_out);
  not not_17 (not_17_out, w_3);
  not not_18 (not_18_out, x_3);
  not not_19 (not_19_out, y_3);
  not not_20 (not_20_out, z_3);
  not not_21 (not_21_out, w_6);
  not not_22 (not_22_out, x_6);
  not not_23 (not_23_out, y_6);
  not not_24 (not_24_out, z_6);
  not not_25 (not_25_out, w_10);
  not not_26 (not_26_out, x_10);
  not not_27 (not_27_out, y_10);
  not not_28 (not_28_out, z_10);
  not not_29 (not_29_out, w_8);
  not not_30 (not_30_out, x_8);
  not not_31 (not_31_out, y_8);
  not not_32 (not_32_out, z_8);
  and and_19 (and_19_out, not_17_out, not_18_out, not_19_out, z_3);
  and and_20 (and_20_out, not_17_out, x_3, not_20_out);
  and and_21 (and_21_out, not_17_out, x_3, y_3);
  and and_22 (and_22_out, w_3, x_3, not_19_out);
  and and_23 (and_23_out, w_3, not_18_out, y_3);
  and and_24 (and_24_out, not_21_out, not_23_out, z_6);
  and and_25 (and_25_out, w_6, y_6, not_24_out);
  and and_26 (and_26_out, w_6, x_6, not_24_out);
  and and_27 (and_27_out, not_22_out, not_23_out, z_6);
  and and_28 (and_28_out, not_25_out, x_10, not_27_out, z_10);
  and and_29 (and_29_out, w_10, not_26_out, not_28_out);
  and and_30 (and_30_out, w_10, not_26_out, y_10);
  and and_31 (and_31_out, w_10, y_10, not_28_out);
  and and_32 (and_32_out, not_26_out, y_10, not_28_out);
  and and_33 (and_33_out, not_29_out, not_30_out, y_8);
  and and_34 (and_34_out, w_8, not_31_out);
  and and_35 (and_35_out, x_8, y_8, not_32_out);
  and and_36 (and_36_out, w_8, not_30_out, z_8);
  or or_5 (out_47, and_19_out, and_20_out, and_21_out, and_22_out, and_23_out);
  or or_6 (F, and_24_out, and_25_out, and_26_out, and_27_out);
  or or_7 (G, and_33_out, and_34_out, and_35_out, and_36_out);
  or or_8 (H, and_28_out, and_29_out, and_30_out, and_31_out, and_32_out);
  not not_33 (not_33_out, w_2);
  not not_34 (not_34_out, x_2);
  not not_35 (not_35_out, y_2);
  not not_36 (not_36_out, z_2);
  and and_37 (and_37_out, w_2, not_35_out);
  and and_38 (and_38_out, w_2, y_2, not_36_out);
  and and_39 (and_39_out, not_33_out, x_2, z_2);
  and and_40 (and_40_out, not_34_out, y_2, not_36_out);
  or or_9 (I, and_37_out, and_38_out, and_39_out, and_40_out);
  // NOT_Gate not_37 has open pins: in=w, out=open
  // NOT_Gate not_38 has open pins: in=x, out=open
  // NOT_Gate not_39 has open pins: in=y, out=open
  // NOT_Gate not_40 has open pins: in=z, out=open
  // NOT_Gate not_41 has open pins: in=w_5, out=open
  // NOT_Gate not_42 has open pins: in=x_5, out=open
  // NOT_Gate not_43 has open pins: in=y_5, out=open
  // NOT_Gate not_44 has open pins: in=z_5, out=open
  // AND_Gate and_41 has open pins: out=and_41_out
  // AND_Gate and_42 has open pins: out=and_42_out
  // AND_Gate and_43 has open pins: out=and_43_out
  // AND_Gate and_44 has open pins: out=and_44_out
  // AND_Gate and_45 has open pins: out=and_45_out
  // AND_Gate and_46 has open pins: out=and_46_out
  // AND_Gate and_47 has open pins: out=and_47_out
  // AND_Gate and_48 has open pins: out=and_48_out
  // AND_Gate and_49 has open pins: out=and_49_out
  or or_10 (out_45, and_41_out, and_42_out, and_43_out, and_44_out, and_45_out);
  or or_11 (out_49, and_46_out, and_47_out, and_48_out, and_49_out);

  // Notes on the sheet:
  //   D
  //   B
  //   C
  //   E
  //   F
endmodule

module A (
  input  w,
  input  x,
  input  y,
  input  z,
  output A
);

  wire and_1_out, and_2_out, and_3_out, and_4_out, and_5_out, not_1_out, not_2_out, not_3_out, not_4_out;

  not not_1 (not_1_out, w);
  not not_2 (not_2_out, x);
  not not_3 (not_3_out, y);
  not not_4 (not_4_out, z);
  and and_1 (and_1_out, w, not_2_out, z);
  and and_2 (and_2_out, w, x, not_4_out);
  and and_3 (and_3_out, not_2_out, not_3_out, not_4_out);
  and and_4 (and_4_out, not_1_out, y, z);
  and and_5 (and_5_out, w, not_3_out);
  or or_1 (A, and_1_out, and_2_out, and_3_out, and_4_out, and_5_out);
endmodule

module B (
  input  w,
  input  x,
  input  y,
  input  z,
  output out_5
);

  wire and_1_out, and_2_out, and_3_out, and_4_out, not_1_out, not_2_out, not_3_out, not_4_out;

  not not_1 (not_1_out, w);
  not not_2 (not_2_out, x);
  not not_3 (not_3_out, y);
  not not_4 (not_4_out, z);
  and and_1 (and_1_out, not_1_out, not_3_out, not_4_out);
  and and_2 (and_2_out, w, y, not_4_out);
  and and_3 (and_3_out, w, not_2_out, y);
  and and_4 (and_4_out, w, not_2_out, not_4_out);
  or or_1 (out_5, and_1_out, and_2_out, and_3_out, and_4_out);

  // Notes on the sheet:
  //   B
endmodule

module C (
  input  w,
  input  x,
  input  y,
  input  z,
  output out_5
);

  wire and_1_out, and_2_out, and_3_out, and_4_out, and_5_out, not_2_out, not_3_out, not_4_out;

  // NOT_Gate not_1 has open pins: in=w, out=open
  not not_2 (not_2_out, x);
  not not_3 (not_3_out, y);
  not not_4 (not_4_out, z);
  and and_1 (and_1_out, w, not_3_out);
  and and_2 (and_2_out, not_2_out, not_3_out, not_4_out);
  and and_3 (and_3_out, x, not_3_out, z);
  and and_4 (and_4_out, w, not_2_out, z);
  and and_5 (and_5_out, x, y, not_4_out);
  or or_1 (out_5, and_1_out, and_2_out, and_3_out, and_4_out, and_5_out);

  // Notes on the sheet:
  //   C
endmodule

module D (
  input  w,
  input  x,
  input  y,
  input  z,
  output out_5
);

  wire and_1_out, and_2_out, and_3_out, and_4_out, not_1_out, not_2_out, not_3_out, not_4_out;

  not not_1 (not_1_out, w);
  not not_2 (not_2_out, x);
  not not_3 (not_3_out, y);
  not not_4 (not_4_out, z);
  and and_1 (and_1_out, not_1_out, not_2_out, z);
  and and_2 (and_2_out, w, y, not_4_out);
  and and_3 (and_3_out, w, x, not_4_out);
  and and_4 (and_4_out, not_2_out, not_3_out, z);
  or or_1 (out_5, and_1_out, and_2_out, and_3_out, and_4_out);

  // Notes on the sheet:
  //   D
endmodule

module E (
  input  w,
  input  x,
  input  y,
  input  z,
  output out_5
);

  wire and_1_out, and_2_out, and_3_out, and_4_out, and_5_out, not_1_out, not_2_out, not_3_out, not_4_out;

  not not_1 (not_1_out, w);
  not not_2 (not_2_out, x);
  not not_3 (not_3_out, y);
  not not_4 (not_4_out, z);
  and and_1 (and_1_out, not_1_out, not_2_out, not_3_out, z);
  and and_2 (and_2_out, not_1_out, x, not_4_out);
  and and_3 (and_3_out, not_1_out, x, y);
  and and_4 (and_4_out, w, x, not_3_out);
  and and_5 (and_5_out, w, not_2_out, y);
  or or_1 (out_5, and_1_out, and_2_out, and_3_out, and_4_out, and_5_out);

  // Notes on the sheet:
  //   E
endmodule

module F (
  input  w,
  input  x,
  input  y,
  input  z,
  output F
);

  wire and_1_out, and_2_out, and_3_out, and_4_out, not_1_out, not_2_out, not_3_out, not_4_out;

  not not_1 (not_1_out, w);
  not not_2 (not_2_out, x);
  not not_3 (not_3_out, y);
  not not_4 (not_4_out, z);
  and and_1 (and_1_out, not_1_out, not_3_out, z);
  and and_2 (and_2_out, w, y, not_4_out);
  and and_3 (and_3_out, w, x, not_4_out);
  and and_4 (and_4_out, not_2_out, not_3_out, z);
  or or_1 (F, and_1_out, and_2_out, and_3_out, and_4_out);

  // Notes on the sheet:
  //   F
endmodule

module G (
  input  w,
  input  x,
  input  y,
  input  z,
  output G
);

  wire and_1_out, and_2_out, and_3_out, and_4_out, not_1_out, not_2_out, not_3_out, not_4_out;

  not not_1 (not_1_out, w);
  not not_2 (not_2_out, x);
  not not_3 (not_3_out, y);
  not not_4 (not_4_out, z);
  and and_1 (and_1_out, not_1_out, not_2_out, y);
  and and_2 (and_2_out, w, not_3_out);
  and and_3 (and_3_out, x, y, not_4_out);
  and and_4 (and_4_out, w, not_2_out, z);
  or or_1 (G, and_1_out, and_2_out, and_3_out, and_4_out);
endmodule

module H (
  input  w,
  input  x,
  input  y,
  input  z,
  output H
);

  wire and_1_out, and_2_out, and_3_out, and_4_out, and_5_out, not_1_out, not_2_out, not_3_out, not_4_out;

  not not_1 (not_1_out, w);
  not not_2 (not_2_out, x);
  not not_3 (not_3_out, y);
  not not_4 (not_4_out, z);
  and and_1 (and_1_out, not_1_out, x, not_3_out, z);
  and and_2 (and_2_out, w, not_2_out, not_4_out);
  and and_3 (and_3_out, w, not_2_out, y);
  and and_4 (and_4_out, w, y, not_4_out);
  and and_5 (and_5_out, not_2_out, y, not_4_out);
  or or_1 (H, and_1_out, and_2_out, and_3_out, and_4_out, and_5_out);
endmodule

module I (
  input  w,
  input  x,
  input  y,
  input  z,
  output I
);

  wire and_1_out, and_2_out, and_3_out, and_4_out, not_1_out, not_2_out, not_3_out, not_4_out;

  not not_1 (not_1_out, w);
  not not_2 (not_2_out, x);
  not not_3 (not_3_out, y);
  not not_4 (not_4_out, z);
  and and_1 (and_1_out, w, not_3_out);
  and and_2 (and_2_out, w, y, not_4_out);
  and and_3 (and_3_out, not_1_out, x, z);
  and and_4 (and_4_out, not_2_out, y, not_4_out);
  or or_1 (I, and_1_out, and_2_out, and_3_out, and_4_out);
endmodule
