// Logisim project template.circ as structural Verilog: 1 circuit, main circuit main
module main (
  input  w,
  input  x,
  input  y,
  input  z
);

  wire and_1_out, and_2_out, and_3_out, and_4_out, and_5_out;

  // NOT_Gate not_1 has open pins: in=w, out=open
  // NOT_Gate not_2 has open pins: in=x, out=open
  // NOT_Gate not_3 has open pins: in=y, out=open
  // NOT_Gate not_4 has open pins: in=z, out=open
  // AND_Gate and_1 has open pins: out=and_1_out
  // AND_Gate and_2 has open pins: out=and_2_out
  // AND_Gate and_3 has open pins: out=and_3_out
  // AND_Gate and_4 has open pins: out=and_4_out
  // AND_Gate and_5 has open pins: out=and_5_out
  // OR_Gate or_1 has open pins: in0=and_1_out, in1=and_2_out, in2=and_3_out, in3=and_4_out, in4=and_5_out, out=open
  // OR_Gate or_2 is placed but not wired
endmodule
