// Logisim project assign2.circ as structural Verilog: 9 circuits, main circuit main
module main (
  input  x
);

  wire clock_1_out, j_k_ff_1_q, j_k_ff_2_q, j_k_ff_3_q, j_k_ff_4_q, ja_1_ja, jb_1_out_6, jc_1_out_6,
       jd_1_out_6, ka_1_out_6, kb_1_out_6, kc_1_out_6, kd_1_out_6;

  JA ja_1 (.B(j_k_ff_2_q), .C(j_k_ff_3_q), .D(j_k_ff_4_q), .x(x), .JA(ja_1_ja), .A(j_k_ff_1_q));
  KA ka_1 (.A(j_k_ff_1_q), .B(j_k_ff_2_q), .C(j_k_ff_3_q), .D(j_k_ff_4_q), .x(x), .out_6(ka_1_out_6));
  JB jb_1 (.A(j_k_ff_1_q), .B(j_k_ff_2_q), .C(j_k_ff_3_q), .D(j_k_ff_4_q), .x(x), .out_6(jb_1_out_6));
  KB kb_1 (.A(j_k_ff_1_q), .B(j_k_ff_2_q), .C(j_k_ff_3_q), .D(j_k_ff_4_q), .x(x), .out_6(kb_1_out_6));
  JC jc_1 (.A(j_k_ff_1_q), .B(j_k_ff_2_q), .C(j_k_ff_3_q), .D(j_k_ff_4_q), .x(x), .out_6(jc_1_out_6));
  KC kc_1 (.A(j_k_ff_1_q), .B(j_k_ff_2_q), .C(j_k_ff_3_q), .D(j_k_ff_4_q), .x(x), .out_6(kc_1_out_6));
  JD jd_1 (.out_6(jd_1_out_6), .A(j_k_ff_1_q), .B(j_k_ff_2_q), .C(j_k_ff_3_q), .D(j_k_ff_4_q), .x(x));
  KD kd_1 (.out_6(kd_1_out_6), .A(j_k_ff_1_q), .B(j_k_ff_2_q), .C(j_k_ff_3_q), .D(j_k_ff_4_q), .x(x));
  Clock clock_1 (.out(clock_1_out));
  J_K_Flip_Flop j_k_ff_1 (
    .J(ja_1_ja), .clk(clock_1_out), .K(ka_1_out_6), .Q(j_k_ff_1_q));  // open: Qn, preset, en, reset
  J_K_Flip_Flop j_k_ff_2 (
    .J(jb_1_out_6), .clk(clock_1_out), .K(kb_1_out_6), .Q(j_k_ff_2_q));  // open: Qn, preset, en, reset
  J_K_Flip_Flop j_k_ff_3 (
    .J(jc_1_out_6), .clk(clock_1_out), .K(kc_1_out_6), .Q(j_k_ff_3_q));  // open: Qn, preset, en, reset
  J_K_Flip_Flop j_k_ff_4 (
    .J(jd_1_out_6), .clk(clock_1_out), .K(kd_1_out_6), .Q(j_k_ff_4_q));  // open: Qn, preset, en, reset
  LED led_1 (.in(j_k_ff_1_q));
  LED led_2 (.in(j_k_ff_2_q));
  LED led_3 (.in(j_k_ff_3_q));
  LED led_4 (.in(j_k_ff_4_q));
  // AND_Gate and_1 is placed but not wired
endmodule

module JA (
  input  A,
  input  B,
  input  C,
  input  D,
  input  x,
  output JA
);

  wire and_1_out, and_2_out, not_1_out, not_2_out, not_3_out, not_4_out, not_5_out;

  not not_1 (not_1_out, B);
  not not_2 (not_2_out, C);
  not not_3 (not_3_out, D);
  not not_4 (not_4_out, D);
  not not_5 (not_5_out, x);
  and and_1 (and_1_out, not_1_out, not_2_out, not_3_out, x);
  and and_2 (and_2_out, B, not_2_out, not_4_out, not_5_out);
  or or_1 (JA, and_1_out, and_2_out);
endmodule

module KA (
  input  A,
  input  B,
  input  C,
  input  D,
  input  x,
  output out_6
);

  wire and_1_out, and_2_out, not_1_out, not_2_out, not_3_out, not_4_out, not_5_out, not_6_out;

  not not_1 (not_1_out, B);
  not not_2 (not_2_out, C);
  not not_3 (not_3_out, D);
  not not_4 (not_4_out, x);
  not not_5 (not_5_out, C);
  not not_6 (not_6_out, D);
  and and_1 (and_1_out, not_1_out, not_2_out, not_3_out, not_4_out);
  and and_2 (and_2_out, B, not_5_out, not_6_out, x);
  or or_1 (out_6, and_1_out, and_2_out);
endmodule

module JB (
  input  A,
  input  B,
  input  C,
  input  D,
  input  x,
  output out_6
);

  wire and_1_out, and_2_out, not_1_out, not_2_out, not_3_out, not_4_out;

  not not_1 (not_1_out, D);
  not not_2 (not_2_out, A);
  not not_3 (not_3_out, D);
  not not_4 (not_4_out, x);
  and and_1 (and_1_out, not_2_out, C, not_3_out, not_4_out);
  and and_2 (and_2_out, A, C, not_1_out, x);
  or or_1 (out_6, and_1_out, and_2_out);
endmodule

module KB (
  input  A,
  input  B,
  input  C,
  input  D,
  input  x,
  output out_6
);

  wire and_1_out, and_2_out, not_1_out, not_2_out, not_3_out, not_4_out;

  not not_1 (not_1_out, A);
  not not_2 (not_2_out, D);
  not not_3 (not_3_out, D);
  not not_4 (not_4_out, x);
  and and_1 (and_1_out, not_1_out, C, not_2_out, x);
  and and_2 (and_2_out, A, C, not_3_out, not_4_out);
  or or_1 (out_6, and_1_out, and_2_out);
endmodule

module JC (
  input  A,
  input  B,
  input  C,
  input  D,
  input  x,
  output out_6
);

  wire and_1_out, and_2_out, and_3_out, and_4_out, not_1_out, not_2_out, not_5_out;

  not not_1 (not_1_out, A);
  not not_2 (not_2_out, B);
  // NOT_Gate not_3 has open pins: in=C, out=open
  // NOT_Gate not_4 has open pins: in=D, out=open
  not not_5 (not_5_out, x);
  and and_1 (and_1_out, not_1_out, not_2_out, D, not_5_out);
  and and_2 (and_2_out, not_1_out, B, D, x);
  and and_3 (and_3_out, A, not_2_out, D, x);
  and and_4 (and_4_out, A, B, D, not_5_out);
  or or_1 (out_6, and_1_out, and_2_out, and_3_out, and_4_out);
endmodule

module KC (
  input  A,
  input  B,
  input  C,
  input  D,
  input  x,
  output out_6
);

  wire and_1_out, and_2_out, and_3_out, and_4_out, not_1_out, not_2_out, not_5_out;

  not not_1 (not_1_out, A);
  not not_2 (not_2_out, B);
  // NOT_Gate not_3 has open pins: in=C, out=open
  // NOT_Gate not_4 has open pins: in=D, out=open
  not not_5 (not_5_out, x);
  and and_1 (and_1_out, not_1_out, not_2_out, D, x);
  and and_2 (and_2_out, not_1_out, B, D, not_5_out);
  and and_3 (and_3_out, A, not_2_out, D, not_5_out);
  and and_4 (and_4_out, A, B, D, x);
  or or_1 (out_6, and_1_out, and_2_out, and_3_out, and_4_out);
endmodule

module JD (
  input  A,
  input  B,
  input  C,
  input  D,
  input  x,
  output out_6
);

  wire and_1_out, and_2_out, and_3_out, and_4_out, and_5_out, and_6_out, and_7_out, and_8_out, not_1_out,
       not_2_out, not_3_out, not_4_out, not_5_out;

  not not_1 (not_1_out, A);
  not not_2 (not_2_out, B);
  not not_3 (not_3_out, C);
  not not_4 (not_4_out, D);
  not not_5 (not_5_out, x);
  and and_1 (and_1_out, not_1_out, not_2_out, not_3_out, not_5_out);
  and and_2 (and_2_out, not_1_out, not_2_out, C, x);
  and and_3 (and_3_out, not_1_out, B, C, not_5_out);
  and and_4 (and_4_out, not_1_out, B, not_3_out, x);
  and and_5 (and_5_out, A, not_2_out, C, not_5_out);
  and and_6 (and_6_out, A, B, C, x);
  and and_7 (and_7_out, A, B, not_3_out, not_5_out);
  and and_8 (and_8_out, A, not_2_out, not_3_out, x);
  or or_1 (out_6, and_1_out, and_2_out, and_3_out, and_4_out, and_5_out, and_6_out, and_7_out, and_8_out);

  // Notes on the sheet:
  //   A
  //   B
  //   C
  //   D
  //   x
endmodule

module KD (
  input  A,
  input  B,
  input  C,
  input  D,
  input  x,
  output out_6
);

  wire and_1_out, and_2_out, and_3_out, and_4_out, and_5_out, and_6_out, and_7_out, and_8_out, not_1_out,
       not_2_out, not_3_out, not_4_out, not_5_out;

  not not_1 (not_1_out, A);
  not not_2 (not_2_out, B);
  not not_3 (not_3_out, C);
  not not_4 (not_4_out, D);
  not not_5 (not_5_out, x);
  and and_1 (and_1_out, not_1_out, not_2_out, not_3_out, x);
  and and_2 (and_2_out, not_1_out, not_2_out, C, not_5_out);
  and and_3 (and_3_out, not_1_out, B, C, x);
  and and_4 (and_4_out, not_1_out, B, not_3_out, not_5_out);
  and and_5 (and_5_out, A, not_2_out, not_3_out, not_5_out);
  and and_6 (and_6_out, A, not_2_out, C, x);
  and and_7 (and_7_out, A, B, C, not_5_out);
  and and_8 (and_8_out, A, B, not_3_out, x);
  or or_1 (out_6, and_1_out, and_2_out, and_3_out, and_4_out, and_5_out, and_6_out, and_7_out, and_8_out);

  // Notes on the sheet:
  //   A
  //   B
  //   C
  //   D
  //   x
endmodule
