// Logisim project question2.circ as structural Verilog: 1 circuit, main circuit main
module main (
  input  in_1
);

  wire A_q, and_1_out, and_2_out, B_q, clock_1_out, not_1_out, not_2_out, or_1_out;

  not not_1 (not_1_out, B_q);
  not not_2 (not_2_out, in_1);
  and and_1 (and_1_out, not_1_out, in_1);
  and and_2 (and_2_out, B_q, not_2_out);
  or or_1 (or_1_out, and_1_out, and_2_out);
  Clock clock_1 (.out(clock_1_out));
  J_K_Flip_Flop A (.J(or_1_out), .clk(clock_1_out), .K(or_1_out), .Q(A_q));  // open: Qn, preset, en, reset
  J_K_Flip_Flop B (.J(1'b1), .clk(clock_1_out), .K(1'b1), .Q(B_q));  // open: Qn, preset, en, reset
  LED led_1 (.in(A_q));
  LED led_2 (.in(B_q));
endmodule
